// Logisim project all.circ as structural Verilog: 2 circuits, main circuit zadanie2
module zadanie2 (
  input  a,
  input  c,
  input  d,
  input  e,
  input  b,
  output f
);

  wire and_1_out, and_2_out, and_3_out, and_4_out, and_5_out, and_6_out, and_7_out, and_8_out, and_9_out,
       and_10_out, not_1_out, not_2_out, not_3_out, not_4_out, or_1_out, or_2_out, or_3_out, or_4_out,
       or_5_out;

  not not_1 (not_1_out, a);
  not not_2 (not_2_out, c);
  not not_3 (not_3_out, d);
  not not_4 (not_4_out, e);
  and and_1 (and_1_out, not_1_out, d);
  and and_2 (and_2_out, c, not_4_out);
  and and_3 (and_3_out, not_2_out, not_3_out);
  and and_4 (and_4_out, a, not_2_out);
  and and_5 (and_5_out, not_3_out, e);
  and and_6 (and_6_out, not_2_out, e);
  and and_7 (and_7_out, not_1_out, c);
  or or_1 (or_1_out, and_1_out, and_2_out);
  and and_8 (and_8_out, and_3_out, e);
  and and_9 (and_9_out, and_4_out, not_3_out);
  or or_2 (or_2_out, and_5_out, and_6_out);
  and and_10 (and_10_out, and_7_out, d);
  or or_3 (or_3_out, and_8_out, and_9_out);
  or or_4 (or_4_out, or_2_out, and_10_out);
  or or_5 (or_5_out, or_1_out, or_3_out);
  Multiplexer multiplexer_1 (.in0(or_5_out), .in1(or_4_out), .out(f));  // open: sel

  // Notes on the sheet:
  //   a
  //   a'
  //   c
  //   c'
  //   d
  //   d'
  //   e
  //   e'
  //   a'd
  //   ce'
  //   d'e
  //   c'e
  //   f(a,b,c,d,e) = b'*f0 + b*f1
  //   c'd'e
  //   ac'd'
  //   a'cd
  //   f1 (b=1)
  //   f0 (b=0)
  //   b: wejscie wyboru (Select)
endmodule

module zadanie1 (
  input  a,
  input  d,
  input  c,
  input  b,
  output f
);

  wire and_1_out, multiplexer_1_out, multiplexer_2_out, nand_1_out, not_1_out, not_2_out, or_1_out;

  not not_1 (not_1_out, a);
  not not_2 (not_2_out, d);
  or or_1 (or_1_out, not_1_out, d);
  and and_1 (and_1_out, a, not_2_out);
  nand nand_1 (nand_1_out, a, d);
  Multiplexer multiplexer_1 (.in0(or_1_out), .in1(and_1_out), .out(multiplexer_1_out), .sel(c));
  Multiplexer multiplexer_2 (.in0(nand_1_out), .in1(not_2_out), .out(multiplexer_2_out), .sel(c));
  Multiplexer multiplexer_3 (.in0(multiplexer_1_out), .in1(multiplexer_2_out), .out(f), .sel(b));

  // Notes on the sheet:
  //   MUX1 = F0 (b=0)
  //   MUX2 = F1 (b=1)
  //   MUX3 (b)
endmodule
